// Logisim project Digital_Stopwatch.circ as structural Verilog: 4 circuits, main circuit main
module main (
  input  in_1,
  input  in_2,
  input  Stop
);

  wire and_1_out, mod_6_1_out_4, mod_6_1_out_5, mod_6_1_out_6, mod_10_1_out_4, mod_10_1_out_5,
       mod_10_1_out_6, mod_10_1_out_7, n7segment_1_out_5, n7segment_1_out_6, n7segment_1_out_7,
       n7segment_1_out_8, n7segment_1_out_9, n7segment_1_out_10, n7segment_1_out_11, n7segment_2_out_5,
       n7segment_2_out_6, n7segment_2_out_7, n7segment_2_out_8, n7segment_2_out_9, n7segment_2_out_10,
       n7segment_2_out_11, not_1_out, not_2_out, Reset_out;

  Button Reset (.out(Reset_out));
  mod_6 mod_6_1 (
    .in_1(in_1), .in_2(and_1_out), .in_3(Reset_out), .out_4(mod_6_1_out_4), .out_5(mod_6_1_out_5),
    .out_6(mod_6_1_out_6));
  _7segment u_7segment_1 (
    .in_1(in_2), .in_2(mod_6_1_out_4), .in_3(mod_6_1_out_5), .in_4(mod_6_1_out_6), .out_5(n7segment_1_out_5),
    .out_6(n7segment_1_out_6), .out_7(n7segment_1_out_7), .out_8(n7segment_1_out_8),
    .out_9(n7segment_1_out_9), .out_10(n7segment_1_out_10), .out_11(n7segment_1_out_11));
  and and_1 (and_1_out, mod_10_1_out_4, not_1_out, not_2_out, mod_10_1_out_7);
  _7_Segment_Display u_7_segment_display_1 (
    .g(n7segment_1_out_11), .f(n7segment_1_out_10), .a(n7segment_1_out_5), .b(n7segment_1_out_6),
    .e(n7segment_1_out_9), .d(n7segment_1_out_8), .c(n7segment_1_out_7));  // open: dp
  mod_10 mod_10_1 (
    .in_1(in_1), .Stop(Stop), .Reset(Reset_out), .out_4(mod_10_1_out_4), .out_5(mod_10_1_out_5),
    .out_6(mod_10_1_out_6), .out_7(mod_10_1_out_7));
  not not_1 (not_1_out, mod_10_1_out_5);
  not not_2 (not_2_out, mod_10_1_out_6);
  _7segment u_7segment_2 (
    .in_1(mod_10_1_out_4), .in_2(mod_10_1_out_5), .in_3(mod_10_1_out_6), .in_4(mod_10_1_out_7),
    .out_5(n7segment_2_out_5), .out_6(n7segment_2_out_6), .out_7(n7segment_2_out_7),
    .out_8(n7segment_2_out_8), .out_9(n7segment_2_out_9), .out_10(n7segment_2_out_10),
    .out_11(n7segment_2_out_11));
  _7_Segment_Display u_7_segment_display_2 (
    .g(n7segment_2_out_11), .f(n7segment_2_out_10), .a(n7segment_2_out_5), .b(n7segment_2_out_6),
    .e(n7segment_2_out_9), .d(n7segment_2_out_8), .c(n7segment_2_out_7));  // open: dp
endmodule

module _7segment (
  input  in_1,
  input  in_2,
  input  in_3,
  input  in_4,
  output out_5,
  output out_6,
  output out_7,
  output out_8,
  output out_9,
  output out_10,
  output out_11
);

  wire and_1_out, and_2_out, and_3_out, and_4_out, and_5_out, and_6_out, and_7_out, and_8_out, and_9_out,
       not_1_out, not_2_out, not_3_out;

  not not_1 (not_1_out, in_2);
  not not_2 (not_2_out, in_4);
  not not_3 (not_3_out, in_3);
  and and_1 (and_1_out, in_4, in_2);
  and and_2 (and_2_out, not_1_out, not_2_out);
  and and_3 (and_3_out, not_3_out, not_2_out);
  and and_4 (and_4_out, in_3, in_4);
  and and_5 (and_5_out, in_3, not_2_out);
  and and_6 (and_6_out, in_2, not_3_out, in_4);
  and and_7 (and_7_out, not_1_out, in_3);
  and and_8 (and_8_out, in_2, not_3_out);
  and and_9 (and_9_out, in_2, not_2_out);
  or or_1 (out_5, and_1_out, and_2_out, in_3, in_1);
  or or_2 (out_6, not_1_out, and_3_out, and_4_out);
  or or_3 (out_7, in_2, not_3_out, in_4);
  or or_4 (out_8, in_1, and_5_out, and_2_out, and_6_out, and_7_out);
  or or_5 (out_9, and_2_out, and_5_out);
  or or_6 (out_10, and_3_out, and_8_out, and_9_out, in_1);
  or or_7 (out_11, and_8_out, and_7_out, and_5_out, in_1);
endmodule

module mod_6 (
  input  in_1,
  input  in_2,
  input  in_3,
  output out_4,
  output out_5,
  output out_6
);

  wire and_1_out, and_2_out, clock_1_out, j_k_ff_3_qn;

  Clock clock_1 (.out(clock_1_out));
  J_K_Flip_Flop j_k_ff_1 (
    .J(in_1), .clk(clock_1_out), .K(in_1), .Q(out_6), .en(in_2), .reset(in_3));  // open: Qn, preset
  and and_1 (and_1_out, j_k_ff_3_qn, out_6);
  J_K_Flip_Flop j_k_ff_2 (
    .J(and_1_out), .clk(clock_1_out), .K(out_6), .Q(out_5), .en(in_2), .reset(in_3));  // open: Qn, preset
  and and_2 (and_2_out, out_6, out_5);
  J_K_Flip_Flop j_k_ff_3 (
    .J(and_2_out), .clk(clock_1_out), .K(out_6), .Q(out_4), .Qn(j_k_ff_3_qn), .en(in_2), .reset(in_3));  // open: preset
endmodule

module mod_10 (
  input  in_1,
  input  Stop,
  input  Reset,
  output out_4,
  output out_5,
  output out_6,
  output out_7
);

  wire and_1_out, and_2_out, and_3_out, clock_1_out, j_k_ff_4_qn;

  Clock clock_1 (.out(clock_1_out));
  J_K_Flip_Flop j_k_ff_1 (
    .J(in_1), .clk(clock_1_out), .K(in_1), .Q(out_7), .en(Stop), .reset(Reset));  // open: Qn, preset
  and and_1 (and_1_out, j_k_ff_4_qn, out_7);
  J_K_Flip_Flop j_k_ff_2 (
    .J(and_1_out), .clk(clock_1_out), .K(out_7), .Q(out_6), .en(Stop), .reset(Reset));  // open: Qn, preset
  and and_2 (and_2_out, out_7, out_6);
  J_K_Flip_Flop j_k_ff_3 (
    .J(and_2_out), .clk(clock_1_out), .K(and_2_out), .Q(out_5), .en(Stop), .reset(Reset));  // open: Qn, preset
  and and_3 (and_3_out, and_2_out, out_5);
  J_K_Flip_Flop j_k_ff_4 (
    .J(and_3_out), .clk(clock_1_out), .K(out_7), .Q(out_4), .Qn(j_k_ff_4_qn), .en(Stop), .reset(Reset));  // open: preset
endmodule
